# Fritzing sketch SEG7_ADCDELAY (saved by Fritzing 0.3.19b)
breadboards: 1

parts:
  Arduino1 = Arduino
  7_Segment = 7-Segment LED Display [package=THT]
  7_Segment_2 = 7-Segment LED Display [package=THT]
  10K = Rotary Potentiometer (Large) [package=THT]
  470 = Resistor [resistance=470 package=THT]
  470_2 = Resistor [resistance=470 package=THT]
  470_3 = Resistor [resistance=470 package=THT]
  470_4 = Resistor [resistance=470 package=THT]
  470_5 = Resistor [resistance=470 package=THT]
  470_6 = Resistor [resistance=470 package=THT]
  470_7 = Resistor [resistance=470 package=THT]
  470_8 = Resistor [resistance=470 package=THT]
  470_9 = Resistor [resistance=470 package=THT]
  470_10 = Resistor [resistance=470 package=THT]
  470_11 = Resistor [resistance=470 package=THT]
  R4 = Resistor [resistance=470 package=THT]
  470_12 = Resistor [resistance=470 package=THT]
  470_13 = Resistor [resistance=470 package=THT]

nets:
  N1: Arduino1.GND, 7_Segment.commAnode#2, 7_Segment_2.commAnode#2, 10K.leg1
  N2: Arduino1.D13, 470_4.Pin_0
  N3: Arduino1.D12, 470_5.Pin_0
  N4: Arduino1.D11, 470_12.Pin_0
  N5: Arduino1.D10, R4.Pin_0
  N6: Arduino1.D9, 470_13.Pin_1
  N7: Arduino1.D8, 470_7.Pin_0
  N8: Arduino1.D7, 470_6.Pin_0
  N9: Arduino1.D6, 470_11.Pin_1
  N10: Arduino1.D5, 470_9.Pin_1
  N11: Arduino1.D4, 470_10.Pin_1
  N12: Arduino1.D3, 470_8.Pin_1
  N13: Arduino1.D2, 470_3.Pin_1
  N14: Arduino1.D1TX, 470.Pin_1
  N15: Arduino1.D0RX, 470_2.Pin_1
  N16: Arduino1.+5V, 10K.leg2
  N17: Arduino1.A0, 10K.wiper
  N18: 7_Segment.cathodeE, 470_10.Pin_0
  N19: 7_Segment.cathodeD, 470_8.Pin_0
  N20: 7_Segment.cathodeC, 470_3.Pin_0
  N21: 7_Segment.cathodeB, 470.Pin_0
  N22: 7_Segment.cathodeA, 470_2.Pin_0
  N23: 7_Segment.cathodeF, 470_9.Pin_0
  N24: 7_Segment.cathodeG, 470_11.Pin_0
  N25: 7_Segment_2.cathodeE, 470_12.Pin_1
  N26: 7_Segment_2.cathodeD, R4.Pin_1
  N27: 7_Segment_2.cathodeC, 470_13.Pin_0
  N28: 7_Segment_2.cathodeB, 470_7.Pin_1
  N29: 7_Segment_2.cathodeA, 470_6.Pin_1
  N30: 7_Segment_2.cathodeF, 470_5.Pin_1
  N31: 7_Segment_2.cathodeG, 470_4.Pin_1
